// Logisim project processeur.circ as structural Verilog: 11 circuits, main circuit main
module main (
  input  Reset,
  input  ResetRAM
);

  wire CALL, Clock, Clock_out, Cond, CTRL, Exec, Fetch, getcst_1_imm, Load, ramctrl_1_memload,
       ramctrl_1_memstore, RET, Store, WriteReg;
  wire [2:0] GetOp;
  wire [15:0] Addr, alu_1_output, getcst_1_cst, JMP_Address, MemIN, PC, R0, R1, R2, R3, R4, R5, R6, R7, SR1,
       SR2;
  wire [31:0] bit_extender_1_out, IR, MemOUT;

  Clock u_Clock (.out(Clock_out));
  Seq seq_1 (.ClockOrig(Clock_out), .reset(Reset), .Fetch(Fetch), .Exec(Exec), .Clock(Clock));
  LED led_1 (.in(Clock_out));
  RegPC regpc_1 (
    .JMP_Address(JMP_Address), .Cond(Cond), .CTRL(CTRL), .Exec(Exec), .Reset(Reset), .PC(PC), .CALL(CALL),
    .RET(RET), .Clock(Clock));
  // Probe on PC
  GetAddr getaddr_1 (.PC(PC), .Addr(Addr), .Fetch(Fetch), .Load(Load), .Store(Store), .SR1(SR1));
  // Probe on Addr
  LED led_2 (.in(Fetch));
  LED led_3 (.in(Exec));
  // Probe on MemIN
  assign bit_extender_1_out = {{16{MemIN[15]}}, MemIN};  // Bit_Extender bit_extender_1
  // Probe on PC
  // Probe on IR
  DecodeIR decodeir_1 (
    .CTRL(CTRL), .WriteReg(WriteReg), .IR(IR), .Load(Load), .GetOp(GetOp), .JMPAddress(JMP_Address),
    .Store(Store), .RET(RET), .CALL(CALL));
  RamCtrl ramctrl_1 (
    .Store(Store), .Fetch(Fetch), .Exec(Exec), .Load(Load), .MemStore(ramctrl_1_memstore),
    .MemLoad(ramctrl_1_memload), .Clock(Clock));
  // Probe on MemOUT
  RAM #(.addrWidth(16), .dataWidth(32), .bus("separate")) ram_1 (
    .addr(Addr), .din(bit_extender_1_out), .data(MemOUT), .str(ramctrl_1_memstore), .clk(ramctrl_1_memstore),
    .ld(ramctrl_1_memload), .clr(ResetRAM));  // open: sel
  // Probe on R0
  // Probe on R3
  // Probe on R6
  Register #(.width(32), .trigger("falling")) RegIR (.D(MemOUT), .Q(IR), .clk(Fetch), .clr(Reset));  // open: en
  // Probe on R1
  // Probe on R4
  // Probe on R7
  // Probe on IR
  // Probe on R2
  // Probe on R5
  // Probe on IR[8:6]
  // Probe on IR[11:9]
  // Probe on IR[14:12]
  // Probe on getcst_1_cst
  GetCst getcst_1 (.IR(IR), .Cst(getcst_1_cst), .Imm(getcst_1_imm));
  Registres registres_1 (
    .SR1(IR[11:9]), .IN(alu_1_output), .SR2(IR[14:12]), .WriteReg(WriteReg), .DR(IR[8:6]), .OUT_SR1(SR1),
    .OUT_SR2(SR2), .OUT_DR(MemIN), .R0(R0), .R1(R1), .R2(R2), .R3(R3), .R4(R4), .R5(R5), .R6(R6), .R7(R7),
    .Reset(Reset), .Clock(Exec), .INLoad(MemOUT), .Load(Load));
  // Probe on SR1
  // Probe on SR2
  ALU alu_1 (.Imm(getcst_1_imm), .e2(GetOp), .Input1(SR1), .Input2(SR2), .Output(alu_1_output), .Cst(getcst_1_cst));
  // Probe on alu_1_output
  // Probe on R0
  // Probe on R1
  // Probe on R2
  // Probe on R3
  // Probe on R4
  // Probe on R5
  // Probe on R6
  // Probe on R7
  // Probe on alu_1_output
  CondCTRL condctrl_1 (.CTRL(CTRL), .GetOP(GetOp), .SR1(SR1), .SR2(SR2), .Cond(Cond));

  // Notes on the sheet:
  //   RAM
  //   CondCTRL
endmodule

module ALU (
  input  [15:0] Input2,
  input  [15:0] Cst,
  input  [15:0] Input1,
  input  Imm,
  input  [2:0] e2,
  output [15:0] Output
);

  wire [3:0] bitselector_1_out;
  wire [15:0] adder_1_out, and_1_out, divider_1_out, multiplexer_1_out, or_1_out, shifter_1_out,
       shifter_2_out, subtractor_1_out, xor_1_out;

  Multiplexer #(.width(16)) multiplexer_1 (.in0(Input2), .in1(Cst), .out(multiplexer_1_out), .sel(Imm));  // open: en
  Adder #(.width(16)) adder_1 (.a(Input1), .b(multiplexer_1_out), .out(adder_1_out));  // open: cin, cout
  assign and_1_out = multiplexer_1_out & Input1;  // AND_Gate and_1, 16 bits wide
  assign or_1_out = multiplexer_1_out | Input1;  // OR_Gate or_1, 16 bits wide
  Subtractor #(.width(16)) subtractor_1 (.a(Input1), .b(multiplexer_1_out), .out(subtractor_1_out));  // open: bin, bout
  Multiplexer #(.select(3), .width(16)) multiplexer_2 (
    .in0(adder_1_out), .in1(subtractor_1_out), .in2(and_1_out), .in3(or_1_out), .in4(xor_1_out),
    .in5(shifter_1_out), .in6(shifter_2_out), .in7(divider_1_out), .out(Output), .sel(e2));  // open: en
  assign xor_1_out = multiplexer_1_out ^ Input1;  // XOR_Gate xor_1, 16 bits wide
  BitSelector #(.width(16), .group(4)) bitselector_1 (.in(multiplexer_1_out), .out(bitselector_1_out), .sel(2'b00));
  Shifter #(.width(16)) shifter_1 (.in(Input1), .\dist (bitselector_1_out), .out(shifter_1_out));
  Divider #(.width(16)) divider_1 (.a(Input1), .b(multiplexer_1_out), .out(divider_1_out));  // open: upper, rem
  Shifter #(.width(16), .shift("lr")) shifter_2 (.in(Input1), .\dist (bitselector_1_out), .out(shifter_2_out));
endmodule

module DecodeIR (
  input  [31:0] IR,
  output WriteReg,
  output Store,
  output Load,
  output CTRL,
  output [2:0] GetOp,
  output [15:0] JMPAddress,
  output RET,
  output CALL
);

  wire decoder_1_out0, decoder_1_out1;

  Decoder #(.select(2), .enable("false")) decoder_1 (
    .out0(decoder_1_out0), .out1(decoder_1_out1), .out3(CTRL), .sel(IR[1:0]));  // open: out2
  assign JMPAddress = CTRL ? IR[31:16] : 16'bz;  // Controlled_Buffer controlled_buffer_1
  Decoder #(.select(3), .disabled(0)) decoder_2 (
    .out0(Store), .out1(Load), .sel(IR[4:2]), .en(decoder_1_out1));  // open: out2, out3, out4, out5, out6, out7
  Decoder #(.select(3), .disabled(0)) decoder_3 (
    .out5(RET), .out6(CALL), .sel(IR[4:2]), .en(CTRL));  // open: out0, out1, out2, out3, out4, out7
  or or_1 (WriteReg, decoder_1_out0, Load);

  assign GetOp = IR[4:2];
endmodule

module GetAddr (
  input  [15:0] PC,
  input  Load,
  input  Store,
  input  Fetch,
  input  [15:0] SR1,
  output [15:0] Addr
);

  wire and_1_out, not_1_out, or_1_out;

  or or_1 (or_1_out, Load, Store);
  not not_1 (not_1_out, Fetch);
  assign Addr = Fetch ? PC : 16'bz;  // Controlled_Buffer controlled_buffer_1
  and and_1 (and_1_out, or_1_out, not_1_out);
  assign Addr = and_1_out ? SR1 : 16'bz;  // Controlled_Buffer controlled_buffer_2
endmodule

module GetCst (
  input  [31:0] IR,
  output [15:0] Cst,
  output Imm
);


  assign Cst = IR[31:16];
  assign Imm = IR[5];
endmodule

module RamCtrl (
  input  Clock,
  input  Exec,
  input  Fetch,
  input  Load,
  input  Store,
  output MemLoad,
  output MemStore
);

  wire and_1_out;

  and and_1 (and_1_out, Exec, Load);
  and and_2 (MemStore, Exec, Clock, Store);
  or or_1 (MemLoad, Fetch, and_1_out);
endmodule

module Registres (
  input  [31:0] INLoad,
  input  Load,
  input  [15:0] IN,
  input  [2:0] SR1,
  input  [2:0] SR2,
  input  [2:0] DR,
  input  WriteReg,
  input  Clock,
  input  Reset,
  output [15:0] R0,
  output [15:0] R1,
  output [15:0] OUT_SR1,
  output [15:0] R2,
  output [15:0] R3,
  output [15:0] OUT_SR2,
  output [15:0] R4,
  output [15:0] OUT_DR,
  output [15:0] R5,
  output [15:0] R6,
  output [15:0] R7
);

  wire decoder_1_out0, decoder_1_out1, decoder_1_out2, decoder_1_out3, decoder_1_out4, decoder_1_out5,
       decoder_1_out6, decoder_1_out7, not_1_out;
  wire [15:0] controlled_buffer_1_out, controlled_buffer_3_out, controlled_buffer_4_out,
       controlled_buffer_5_out, controlled_buffer_6_out, controlled_buffer_7_out, controlled_buffer_8_out,
       controlled_buffer_9_out, controlled_buffer_10_out;

  not not_1 (not_1_out, Load);
  assign controlled_buffer_1_out = not_1_out ? IN : 16'bz;  // Controlled_Buffer controlled_buffer_1
  assign controlled_buffer_1_out = Load ? INLoad[15:0] : 16'bz;  // Controlled_Buffer controlled_buffer_2
  Decoder #(.select(3)) decoder_1 (
    .out0(decoder_1_out0), .out1(decoder_1_out1), .out2(decoder_1_out2), .out3(decoder_1_out3),
    .out4(decoder_1_out4), .out5(decoder_1_out5), .out6(decoder_1_out6), .out7(decoder_1_out7), .sel(DR),
    .en(WriteReg));
  Register #(.width(16), .trigger("falling")) u_R0 (
    .D(controlled_buffer_3_out), .Q(R0), .clk(Clock), .clr(Reset));  // open: en
  assign controlled_buffer_3_out = decoder_1_out0 ? controlled_buffer_1_out : 16'bz;  // Controlled_Buffer controlled_buffer_3
  assign controlled_buffer_4_out = decoder_1_out1 ? controlled_buffer_1_out : 16'bz;  // Controlled_Buffer controlled_buffer_4
  Register #(.width(16), .trigger("falling")) u_R1 (
    .D(controlled_buffer_4_out), .Q(R1), .clk(Clock), .clr(Reset));  // open: en
  assign controlled_buffer_5_out = decoder_1_out2 ? controlled_buffer_1_out : 16'bz;  // Controlled_Buffer controlled_buffer_5
  Register #(.width(16), .trigger("falling")) u_R2 (
    .D(controlled_buffer_5_out), .Q(R2), .clk(Clock), .clr(Reset));  // open: en
  Register #(.width(16), .trigger("falling")) u_R3 (
    .D(controlled_buffer_6_out), .Q(R3), .clk(Clock), .clr(Reset));  // open: en
  assign controlled_buffer_6_out = decoder_1_out3 ? controlled_buffer_1_out : 16'bz;  // Controlled_Buffer controlled_buffer_6
  Register #(.width(16), .trigger("falling")) u_R4 (
    .D(controlled_buffer_7_out), .Q(R4), .clk(Clock), .clr(Reset));  // open: en
  assign controlled_buffer_7_out = decoder_1_out4 ? controlled_buffer_1_out : 16'bz;  // Controlled_Buffer controlled_buffer_7
  assign controlled_buffer_8_out = decoder_1_out5 ? controlled_buffer_1_out : 16'bz;  // Controlled_Buffer controlled_buffer_8
  Register #(.width(16), .trigger("falling")) u_R5 (
    .D(controlled_buffer_8_out), .Q(R5), .clk(Clock), .clr(Reset));  // open: en
  Register #(.width(16), .trigger("falling")) u_R6 (
    .D(controlled_buffer_9_out), .Q(R6), .clk(Clock), .clr(Reset));  // open: en
  assign controlled_buffer_9_out = decoder_1_out6 ? controlled_buffer_1_out : 16'bz;  // Controlled_Buffer controlled_buffer_9
  Register #(.width(16), .trigger("falling")) u_R7 (
    .D(controlled_buffer_10_out), .Q(R7), .clk(Clock), .clr(Reset));  // open: en
  assign controlled_buffer_10_out = decoder_1_out7 ? controlled_buffer_1_out : 16'bz;  // Controlled_Buffer controlled_buffer_10
  Multiplexer #(.select(3), .width(16), .enable("false")) multiplexer_1 (
    .in0(R0), .in1(R1), .in2(R2), .in3(R3), .in4(R4), .in5(R5), .in6(R6), .in7(R7), .out(OUT_SR1), .sel(SR1));
  Multiplexer #(.select(3), .width(16), .enable("false")) multiplexer_2 (
    .in0(R0), .in1(R1), .in2(R2), .in3(R3), .in4(R4), .in5(R5), .in6(R6), .in7(R7), .out(OUT_SR2), .sel(SR2));
  Multiplexer #(.select(3), .width(16), .enable("false")) multiplexer_3 (
    .in0(R0), .in1(R1), .in2(R2), .in3(R3), .in4(R4), .in5(R5), .in6(R6), .in7(R7), .out(OUT_DR), .sel(DR));
endmodule

module RegPC (
  input  [15:0] JMP_Address,
  input  Cond,
  input  CTRL,
  input  Exec,
  input  Reset,
  input  CALL,
  input  RET,
  input  Clock,
  output [15:0] PC
);

  wire and_1_out, not_1_out, not_2_out, or_1_out;
  wire [15:0] adder_1_out, controlled_buffer_1_out, controlled_buffer_3_out, PILE_output;

  assign controlled_buffer_1_out = or_1_out ? JMP_Address : 16'bz;  // Controlled_Buffer controlled_buffer_1
  or or_1 (or_1_out, Cond, CALL);
  assign controlled_buffer_1_out = not_1_out ? adder_1_out : 16'bz;  // Controlled_Buffer controlled_buffer_2
  Adder #(.width(16)) adder_1 (.a(controlled_buffer_3_out), .b(16'h1), .out(adder_1_out));  // open: cin, cout
  not not_1 (not_1_out, or_1_out);
  Register #(.width(16), .trigger("falling")) u_PC (
    .D(controlled_buffer_1_out), .Q(PC), .clk(Exec), .clr(Reset));  // open: en
  not not_2 (not_2_out, RET);
  assign controlled_buffer_3_out = not_2_out ? PC : 16'bz;  // Controlled_Buffer controlled_buffer_3
  assign controlled_buffer_3_out = RET ? PILE_output : 16'bz;  // Controlled_Buffer controlled_buffer_4
  Pile PILE (.Address_in(PC), .CALL(CALL), .RET(RET), .Clock(and_1_out), .Output(PILE_output), .Reset(Reset));
  and and_1 (and_1_out, Exec, Clock);
endmodule

module Seq (
  input  ClockOrig,
  input  reset,
  output Fetch,
  output Exec,
  output Clock
);

  Register #(.width(1), .trigger("falling")) register_1 (
    .D(Fetch), .Q(Exec), .clk(ClockOrig), .clr(reset));  // open: en
  not not_1 (Fetch, Exec);
  buf buffer_1 (Clock, ClockOrig);
endmodule

module CondCTRL (
  input  CTRL,
  input  [2:0] GetOP,
  input  [15:0] SR1,
  input  [15:0] SR2,
  output Cond
);

  wire and_1_out, and_2_out, and_3_out, and_4_out, comparator_1_eq, comparator_1_gt, comparator_1_lt,
       decoder_1_out0, decoder_1_out1, decoder_1_out2, decoder_1_out3, decoder_1_out4, not_1_out;

  Decoder #(.select(3), .disabled(0)) decoder_1 (
    .out0(decoder_1_out0), .out1(decoder_1_out1), .out2(decoder_1_out2), .out3(decoder_1_out3),
    .out4(decoder_1_out4), .sel(GetOP), .en(CTRL));  // open: out5, out6, out7
  Comparator #(.width(16)) comparator_1 (
    .a(SR1), .b(SR2), .gt(comparator_1_gt), .eq(comparator_1_eq), .lt(comparator_1_lt));
  not not_1 (not_1_out, comparator_1_eq);
  and and_1 (and_1_out, decoder_1_out1, comparator_1_eq);
  and and_2 (and_2_out, decoder_1_out2, not_1_out);
  and and_3 (and_3_out, decoder_1_out3, comparator_1_gt);
  and and_4 (and_4_out, decoder_1_out4, comparator_1_lt);
  or or_1 (Cond, decoder_1_out0, and_1_out, and_2_out, and_3_out, and_4_out);
endmodule

module Pile (
  input  CALL,
  input  RET,
  input  [15:0] Address_in,
  input  Clock,
  input  Reset,
  output [15:0] Output
);

  wire or_1_out;
  wire [15:0] counter_1_q;

  or or_1 (or_1_out, CALL, RET);
  Counter #(.width(16), .max('hffff)) counter_1 (
    .load(RET), .count(or_1_out), .Q(counter_1_q), .clk(Clock), .clr(Reset));  // open: D, carry
  RAM #(.addrWidth(16), .dataWidth(16), .bus("separate")) ram_1 (
    .addr(counter_1_q), .din(Address_in), .data(Output), .str(CALL), .clk(Clock), .ld(RET), .clr(Reset));  // open: sel
endmodule
